// Logisim project my_ram.circ as structural Verilog: 3 circuits, main circuit my_RAM
module bit_ram (
  input  select_value,
  input  input_value,
  input  is_write,
  output output_value
);

  wire and_1_out, and_2_out, not_1_out, not_2_out, not_3_out, not_4_out, or_1_out, or_2_out;

  not not_1 (not_1_out, input_value);
  and and_1 (and_1_out, select_value, not_1_out, is_write);
  and and_2 (and_2_out, select_value, input_value, is_write);
  or or_1 (or_1_out, and_1_out, not_3_out);
  or or_2 (or_2_out, not_2_out, and_2_out);
  not not_2 (not_2_out, or_1_out);
  not not_3 (not_3_out, or_2_out);
  not not_4 (not_4_out, is_write);
  and and_3 (output_value, select_value, not_2_out, not_4_out);
endmodule

module byte_ram (
  input  select_value,
  input  is_write,
  input  a0,
  input  a1,
  input  a2,
  input  a3,
  input  a4,
  input  a5,
  input  a6,
  input  a7,
  output o0,
  output o1,
  output o2,
  output o3,
  output o4,
  output o5,
  output o6,
  output o7
);

  bit_ram bit_ram_1 (.select_value(select_value), .input_value(a0), .is_write(is_write), .output_value(o0));
  bit_ram bit_ram_2 (.select_value(select_value), .input_value(a1), .is_write(is_write), .output_value(o1));
  bit_ram bit_ram_3 (.select_value(select_value), .input_value(a2), .is_write(is_write), .output_value(o2));
  bit_ram bit_ram_4 (.select_value(select_value), .input_value(a3), .is_write(is_write), .output_value(o3));
  bit_ram bit_ram_5 (.select_value(select_value), .input_value(a4), .is_write(is_write), .output_value(o4));
  bit_ram bit_ram_6 (.select_value(select_value), .input_value(a5), .is_write(is_write), .output_value(o5));
  bit_ram bit_ram_7 (.select_value(select_value), .input_value(a6), .is_write(is_write), .output_value(o6));
  bit_ram bit_ram_8 (.select_value(select_value), .input_value(a7), .is_write(is_write), .output_value(o7));
endmodule

module my_RAM (
  input  is_write,
  input  a0,
  input  a1,
  input  a2,
  input  a3,
  input  a4,
  input  a5,
  input  a6,
  input  a7
);

  byte_ram byte_ram_1 (
    .a0(a0), .a1(a1), .a2(a2), .a3(a3), .a4(a4), .a5(a5), .a6(a6), .a7(a7));  // open: select_value, is_write, o0, o1, o2, o3, o4, o5, o6, o7
  byte_ram byte_ram_2 (
    .a0(a0), .a1(a1), .a2(a2), .a3(a3), .a4(a4), .a5(a5), .a6(a6), .a7(a7));  // open: select_value, is_write, o0, o1, o2, o3, o4, o5, o6, o7
  byte_ram byte_ram_3 (
    .a0(a0), .a1(a1), .a2(a2), .a3(a3), .a4(a4), .a5(a5), .a6(a6), .a7(a7));  // open: select_value, is_write, o0, o1, o2, o3, o4, o5, o6, o7
  byte_ram byte_ram_4 (
    .a0(a0), .a1(a1), .a2(a2), .a3(a3), .a4(a4), .a5(a5), .a6(a6), .a7(a7));  // open: select_value, is_write, o0, o1, o2, o3, o4, o5, o6, o7
  byte_ram byte_ram_5 (
    .a0(a0), .a1(a1), .a2(a2), .a3(a3), .a4(a4), .a5(a5), .a6(a6), .a7(a7));  // open: select_value, is_write, o0, o1, o2, o3, o4, o5, o6, o7
  byte_ram byte_ram_6 (
    .a0(a0), .a1(a1), .a2(a2), .a3(a3), .a4(a4), .a5(a5), .a6(a6), .a7(a7));  // open: select_value, is_write, o0, o1, o2, o3, o4, o5, o6, o7
  byte_ram byte_ram_7 (
    .a0(a0), .a1(a1), .a2(a2), .a3(a3), .a4(a4), .a5(a5), .a6(a6), .a7(a7));  // open: select_value, is_write, o0, o1, o2, o3, o4, o5, o6, o7
  byte_ram byte_ram_8 (
    .a0(a0), .a1(a1), .a2(a2), .a3(a3), .a4(a4), .a5(a5), .a6(a6), .a7(a7));  // open: select_value, is_write, o0, o1, o2, o3, o4, o5, o6, o7
  byte_ram byte_ram_9 (
    .a0(a0), .a1(a1), .a2(a2), .a3(a3), .a4(a4), .a5(a5), .a6(a6), .a7(a7));  // open: select_value, is_write, o0, o1, o2, o3, o4, o5, o6, o7
  byte_ram byte_ram_10 (
    .a0(a0), .a1(a1), .a2(a2), .a3(a3), .a4(a4), .a5(a5), .a6(a6), .a7(a7));  // open: select_value, is_write, o0, o1, o2, o3, o4, o5, o6, o7
  byte_ram byte_ram_11 ();  // open: select_value, is_write, a0, a1, a2, a3, a4, a5, a6, a7, o0, o1, o2, o3, o4, o5, o6, o7
  byte_ram byte_ram_12 ();  // open: select_value, is_write, a0, a1, a2, a3, a4, a5, a6, a7, o0, o1, o2, o3, o4, o5, o6, o7
  byte_ram byte_ram_13 ();  // open: select_value, is_write, a0, a1, a2, a3, a4, a5, a6, a7, o0, o1, o2, o3, o4, o5, o6, o7
  byte_ram byte_ram_14 ();  // open: select_value, is_write, a0, a1, a2, a3, a4, a5, a6, a7, o0, o1, o2, o3, o4, o5, o6, o7
  byte_ram byte_ram_15 ();  // open: select_value, is_write, a0, a1, a2, a3, a4, a5, a6, a7, o0, o1, o2, o3, o4, o5, o6, o7
  byte_ram byte_ram_16 ();  // open: select_value, is_write, a0, a1, a2, a3, a4, a5, a6, a7, o0, o1, o2, o3, o4, o5, o6, o7
  byte_ram byte_ram_17 ();  // open: select_value, is_write, a0, a1, a2, a3, a4, a5, a6, a7, o0, o1, o2, o3, o4, o5, o6, o7
  byte_ram byte_ram_18 ();  // open: select_value, is_write, a0, a1, a2, a3, a4, a5, a6, a7, o0, o1, o2, o3, o4, o5, o6, o7
  byte_ram byte_ram_19 ();  // open: select_value, is_write, a0, a1, a2, a3, a4, a5, a6, a7, o0, o1, o2, o3, o4, o5, o6, o7
  byte_ram byte_ram_20 ();  // open: select_value, is_write, a0, a1, a2, a3, a4, a5, a6, a7, o0, o1, o2, o3, o4, o5, o6, o7
  byte_ram byte_ram_21 ();  // open: select_value, is_write, a0, a1, a2, a3, a4, a5, a6, a7, o0, o1, o2, o3, o4, o5, o6, o7
  byte_ram byte_ram_22 ();  // open: select_value, is_write, a0, a1, a2, a3, a4, a5, a6, a7, o0, o1, o2, o3, o4, o5, o6, o7
  byte_ram byte_ram_23 ();  // open: select_value, is_write, a0, a1, a2, a3, a4, a5, a6, a7, o0, o1, o2, o3, o4, o5, o6, o7
  byte_ram byte_ram_24 ();  // open: select_value, is_write, a0, a1, a2, a3, a4, a5, a6, a7, o0, o1, o2, o3, o4, o5, o6, o7
  byte_ram byte_ram_25 ();  // open: select_value, is_write, a0, a1, a2, a3, a4, a5, a6, a7, o0, o1, o2, o3, o4, o5, o6, o7
  byte_ram byte_ram_26 ();  // open: select_value, is_write, a0, a1, a2, a3, a4, a5, a6, a7, o0, o1, o2, o3, o4, o5, o6, o7
  byte_ram byte_ram_27 ();  // open: select_value, is_write, a0, a1, a2, a3, a4, a5, a6, a7, o0, o1, o2, o3, o4, o5, o6, o7
  byte_ram byte_ram_28 ();  // open: select_value, is_write, a0, a1, a2, a3, a4, a5, a6, a7, o0, o1, o2, o3, o4, o5, o6, o7
  byte_ram byte_ram_29 ();  // open: select_value, is_write, a0, a1, a2, a3, a4, a5, a6, a7, o0, o1, o2, o3, o4, o5, o6, o7
  byte_ram byte_ram_30 ();  // open: select_value, is_write, a0, a1, a2, a3, a4, a5, a6, a7, o0, o1, o2, o3, o4, o5, o6, o7
endmodule
