// Logisim project alu.circ as structural Verilog: 7 circuits, main circuit ALU
module summator (
  input  c0,
  input  [15:0] a,
  input  [15:0] b,
  output [15:0] s,
  output c15,
  output c16
);

  wire bit_summator_1_count, bit_summator_2_count, bit_summator_3_count, bit_summator_4_count,
       bit_summator_5_count, bit_summator_6_count, bit_summator_7_count, bit_summator_8_count,
       bit_summator_9_count, bit_summator_10_count, bit_summator_11_count, bit_summator_12_count,
       bit_summator_13_count, bit_summator_14_count;

  bit_summator bit_summator_1 (.a(a[0]), .b(b[0]), .cin(c0), .s(s[0]), .count(bit_summator_1_count));
  bit_summator bit_summator_2 (.a(a[1]), .b(b[1]), .cin(bit_summator_1_count), .s(s[1]), .count(bit_summator_2_count));
  bit_summator bit_summator_3 (.a(a[2]), .b(b[2]), .cin(bit_summator_2_count), .s(s[2]), .count(bit_summator_3_count));
  bit_summator bit_summator_4 (.a(a[3]), .b(b[3]), .cin(bit_summator_3_count), .s(s[3]), .count(bit_summator_4_count));
  bit_summator bit_summator_5 (.a(a[4]), .b(b[4]), .cin(bit_summator_4_count), .s(s[4]), .count(bit_summator_5_count));
  bit_summator bit_summator_6 (.a(a[5]), .b(b[5]), .cin(bit_summator_5_count), .s(s[5]), .count(bit_summator_6_count));
  bit_summator bit_summator_7 (.a(a[6]), .b(b[6]), .cin(bit_summator_6_count), .s(s[6]), .count(bit_summator_7_count));
  bit_summator bit_summator_8 (.a(a[7]), .b(b[7]), .cin(bit_summator_7_count), .s(s[7]), .count(bit_summator_8_count));
  bit_summator bit_summator_9 (.a(a[8]), .b(b[8]), .cin(bit_summator_8_count), .s(s[8]), .count(bit_summator_9_count));
  bit_summator bit_summator_10 (
    .a(a[9]), .b(b[9]), .cin(bit_summator_9_count), .s(s[9]), .count(bit_summator_10_count));
  bit_summator bit_summator_11 (
    .a(a[10]), .b(b[10]), .cin(bit_summator_10_count), .s(s[10]), .count(bit_summator_11_count));
  bit_summator bit_summator_12 (
    .a(a[11]), .b(b[11]), .cin(bit_summator_11_count), .s(s[11]), .count(bit_summator_12_count));
  bit_summator bit_summator_13 (
    .a(a[12]), .b(b[12]), .cin(bit_summator_12_count), .s(s[12]), .count(bit_summator_13_count));
  bit_summator bit_summator_14 (
    .a(a[13]), .b(b[13]), .cin(bit_summator_13_count), .s(s[13]), .count(bit_summator_14_count));
  bit_summator bit_summator_15 (.a(a[14]), .b(b[14]), .cin(bit_summator_14_count), .s(s[14]), .count(c15));
  bit_summator bit_summator_16 (.a(a[15]), .b(b[15]), .cin(c15), .s(s[15]), .count(c16));
endmodule

module bit_summator (
  input  a,
  input  b,
  input  cin,
  output s,
  output count
);

  wire and_1_out, and_2_out, and_3_out, and_4_out, xor_1_out;

  ExactlyOne xor_1 (.out(xor_1_out), .in0(a), .in1(b), .in2(cin));
  and and_1 (and_1_out, cin, b, a);
  and and_2 (and_2_out, b, a);
  and and_3 (and_3_out, cin, a);
  and and_4 (and_4_out, b, cin);
  or or_1 (s, xor_1_out, and_1_out);
  or or_2 (count, and_2_out, and_3_out, and_4_out);
endmodule

module bit_inverter (
  input  should_change,
  input  \bit ,
  output r
);

  xor xor_1 (r, should_change, \bit );
endmodule

module summator_subtractor (
  input  op,
  input  [15:0] a,
  input  [15:0] b,
  output [15:0] s,
  output Overflow
);

  wire summator_1_c15, summator_1_c16;
  wire [15:0] bit_inverter_1_r;

  bit_inverter bit_inverter_1 (.should_change(op), .\bit (b[0]), .r(bit_inverter_1_r[0]));
  bit_inverter bit_inverter_2 (.should_change(op), .\bit (b[1]), .r(bit_inverter_1_r[1]));
  bit_inverter bit_inverter_3 (.should_change(op), .\bit (b[2]), .r(bit_inverter_1_r[2]));
  bit_inverter bit_inverter_4 (.should_change(op), .\bit (b[3]), .r(bit_inverter_1_r[3]));
  bit_inverter bit_inverter_5 (.should_change(op), .\bit (b[4]), .r(bit_inverter_1_r[4]));
  bit_inverter bit_inverter_6 (.should_change(op), .\bit (b[5]), .r(bit_inverter_1_r[5]));
  bit_inverter bit_inverter_7 (.should_change(op), .\bit (b[6]), .r(bit_inverter_1_r[6]));
  bit_inverter bit_inverter_8 (.should_change(op), .\bit (b[7]), .r(bit_inverter_1_r[7]));
  bit_inverter bit_inverter_9 (.should_change(op), .\bit (b[8]), .r(bit_inverter_1_r[8]));
  bit_inverter bit_inverter_10 (.should_change(op), .\bit (b[9]), .r(bit_inverter_1_r[9]));
  bit_inverter bit_inverter_11 (.should_change(op), .\bit (b[10]), .r(bit_inverter_1_r[10]));
  bit_inverter bit_inverter_12 (.should_change(op), .\bit (b[11]), .r(bit_inverter_1_r[11]));
  bit_inverter bit_inverter_13 (.should_change(op), .\bit (b[12]), .r(bit_inverter_1_r[12]));
  bit_inverter bit_inverter_14 (.should_change(op), .\bit (b[13]), .r(bit_inverter_1_r[13]));
  bit_inverter bit_inverter_15 (.should_change(op), .\bit (b[14]), .r(bit_inverter_1_r[14]));
  bit_inverter bit_inverter_16 (.should_change(op), .\bit (b[15]), .r(bit_inverter_1_r[15]));
  summator summator_1 (.c0(op), .a(a), .b(bit_inverter_1_r), .s(s), .c15(summator_1_c15), .c16(summator_1_c16));
  xor xor_1 (Overflow, summator_1_c16, summator_1_c15);
endmodule

module bit_comparator (
  input  a,
  input  b,
  input  c,
  output is_equal,
  output is_greater,
  output is_shorter
);

  wire and_1_out, and_2_out, not_1_out, not_2_out, not_3_out, xor_1_out;

  xor xor_1 (xor_1_out, a, b);
  and and_1 (and_1_out, a, not_1_out);
  not not_1 (not_1_out, b);
  not not_2 (not_2_out, a);
  not not_3 (not_3_out, xor_1_out);
  and and_2 (and_2_out, not_2_out, b);
  and and_3 (is_equal, not_3_out, c);
  and and_4 (is_greater, and_1_out, c);
  and and_5 (is_shorter, and_2_out, c);

  // Notes on the sheet:
  //   A relation B
endmodule

module bits_comparator (
  input  [15:0] a,
  input  [15:0] b,
  output is_equal,
  output is_greater,
  output is_shorter
);

  wire bit_comparator_1_is_equal, bit_comparator_1_is_greater, bit_comparator_1_is_shorter,
       bit_comparator_2_is_equal, bit_comparator_2_is_greater, bit_comparator_2_is_shorter,
       bit_comparator_3_is_equal, bit_comparator_3_is_greater, bit_comparator_3_is_shorter,
       bit_comparator_4_is_equal, bit_comparator_4_is_greater, bit_comparator_4_is_shorter,
       bit_comparator_5_is_equal, bit_comparator_5_is_greater, bit_comparator_5_is_shorter,
       bit_comparator_6_is_equal, bit_comparator_6_is_greater, bit_comparator_6_is_shorter,
       bit_comparator_7_is_equal, bit_comparator_7_is_greater, bit_comparator_7_is_shorter,
       bit_comparator_8_is_equal, bit_comparator_8_is_greater, bit_comparator_8_is_shorter,
       bit_comparator_9_is_equal, bit_comparator_9_is_greater, bit_comparator_9_is_shorter,
       bit_comparator_10_is_equal, bit_comparator_10_is_greater, bit_comparator_10_is_shorter,
       bit_comparator_11_is_equal, bit_comparator_11_is_greater, bit_comparator_11_is_shorter,
       bit_comparator_12_is_equal, bit_comparator_12_is_greater, bit_comparator_12_is_shorter,
       bit_comparator_13_is_equal, bit_comparator_13_is_greater, bit_comparator_13_is_shorter,
       bit_comparator_14_is_equal, bit_comparator_14_is_greater, bit_comparator_14_is_shorter,
       bit_comparator_15_is_equal, bit_comparator_15_is_greater, bit_comparator_15_is_shorter,
       bit_comparator_16_is_greater, bit_comparator_16_is_shorter;

  bit_comparator bit_comparator_1 (
    .a(a[15]), .b(b[15]), .c(1'b1), .is_equal(bit_comparator_1_is_equal),
    .is_greater(bit_comparator_1_is_greater), .is_shorter(bit_comparator_1_is_shorter));
  bit_comparator bit_comparator_2 (
    .a(a[14]), .b(b[14]), .c(bit_comparator_1_is_equal), .is_equal(bit_comparator_2_is_equal),
    .is_greater(bit_comparator_2_is_greater), .is_shorter(bit_comparator_2_is_shorter));
  bit_comparator bit_comparator_3 (
    .a(a[13]), .b(b[13]), .c(bit_comparator_2_is_equal), .is_equal(bit_comparator_3_is_equal),
    .is_greater(bit_comparator_3_is_greater), .is_shorter(bit_comparator_3_is_shorter));
  bit_comparator bit_comparator_4 (
    .a(a[12]), .b(b[12]), .c(bit_comparator_3_is_equal), .is_equal(bit_comparator_4_is_equal),
    .is_greater(bit_comparator_4_is_greater), .is_shorter(bit_comparator_4_is_shorter));
  bit_comparator bit_comparator_5 (
    .a(a[11]), .b(b[11]), .c(bit_comparator_4_is_equal), .is_equal(bit_comparator_5_is_equal),
    .is_greater(bit_comparator_5_is_greater), .is_shorter(bit_comparator_5_is_shorter));
  bit_comparator bit_comparator_6 (
    .a(a[10]), .b(b[10]), .c(bit_comparator_5_is_equal), .is_equal(bit_comparator_6_is_equal),
    .is_greater(bit_comparator_6_is_greater), .is_shorter(bit_comparator_6_is_shorter));
  bit_comparator bit_comparator_7 (
    .a(a[9]), .b(b[9]), .c(bit_comparator_6_is_equal), .is_equal(bit_comparator_7_is_equal),
    .is_greater(bit_comparator_7_is_greater), .is_shorter(bit_comparator_7_is_shorter));
  bit_comparator bit_comparator_8 (
    .a(a[8]), .b(b[8]), .c(bit_comparator_7_is_equal), .is_equal(bit_comparator_8_is_equal),
    .is_greater(bit_comparator_8_is_greater), .is_shorter(bit_comparator_8_is_shorter));
  bit_comparator bit_comparator_9 (
    .a(a[7]), .b(b[7]), .c(bit_comparator_8_is_equal), .is_equal(bit_comparator_9_is_equal),
    .is_greater(bit_comparator_9_is_greater), .is_shorter(bit_comparator_9_is_shorter));
  bit_comparator bit_comparator_10 (
    .a(a[6]), .b(b[6]), .c(bit_comparator_9_is_equal), .is_equal(bit_comparator_10_is_equal),
    .is_greater(bit_comparator_10_is_greater), .is_shorter(bit_comparator_10_is_shorter));
  bit_comparator bit_comparator_11 (
    .a(a[5]), .b(b[5]), .c(bit_comparator_10_is_equal), .is_equal(bit_comparator_11_is_equal),
    .is_greater(bit_comparator_11_is_greater), .is_shorter(bit_comparator_11_is_shorter));
  bit_comparator bit_comparator_12 (
    .a(a[4]), .b(b[4]), .c(bit_comparator_11_is_equal), .is_equal(bit_comparator_12_is_equal),
    .is_greater(bit_comparator_12_is_greater), .is_shorter(bit_comparator_12_is_shorter));
  bit_comparator bit_comparator_13 (
    .a(a[3]), .b(b[3]), .c(bit_comparator_12_is_equal), .is_equal(bit_comparator_13_is_equal),
    .is_greater(bit_comparator_13_is_greater), .is_shorter(bit_comparator_13_is_shorter));
  bit_comparator bit_comparator_14 (
    .a(a[2]), .b(b[2]), .c(bit_comparator_13_is_equal), .is_equal(bit_comparator_14_is_equal),
    .is_greater(bit_comparator_14_is_greater), .is_shorter(bit_comparator_14_is_shorter));
  bit_comparator bit_comparator_15 (
    .a(a[1]), .b(b[1]), .c(bit_comparator_14_is_equal), .is_equal(bit_comparator_15_is_equal),
    .is_greater(bit_comparator_15_is_greater), .is_shorter(bit_comparator_15_is_shorter));
  bit_comparator bit_comparator_16 (
    .a(a[0]), .b(b[0]), .c(bit_comparator_15_is_equal), .is_equal(is_equal),
    .is_greater(bit_comparator_16_is_greater), .is_shorter(bit_comparator_16_is_shorter));
  or or_1 (is_greater, bit_comparator_16_is_greater, bit_comparator_15_is_greater, bit_comparator_14_is_greater, bit_comparator_13_is_greater, bit_comparator_12_is_greater, bit_comparator_11_is_greater, bit_comparator_10_is_greater, bit_comparator_9_is_greater, bit_comparator_8_is_greater, bit_comparator_7_is_greater, bit_comparator_6_is_greater, bit_comparator_5_is_greater, bit_comparator_4_is_greater, bit_comparator_3_is_greater, bit_comparator_2_is_greater, bit_comparator_1_is_shorter);
  or or_2 (is_shorter, bit_comparator_16_is_shorter, bit_comparator_15_is_shorter, bit_comparator_14_is_shorter, bit_comparator_13_is_shorter, bit_comparator_12_is_shorter, bit_comparator_11_is_shorter, bit_comparator_10_is_shorter, bit_comparator_9_is_shorter, bit_comparator_8_is_shorter, bit_comparator_7_is_shorter, bit_comparator_6_is_shorter, bit_comparator_5_is_shorter, bit_comparator_4_is_shorter, bit_comparator_3_is_shorter, bit_comparator_2_is_shorter, bit_comparator_1_is_greater);
endmodule

module ALU (
  input  OP,
  input  [15:0] a,
  input  [15:0] b,
  output [15:0] result,
  output Overflow,
  output is_equal,
  output is_greater,
  output is_shorter
);

  summator_subtractor summator_subtractor_1 (.op(OP), .a(a), .b(b), .Overflow(Overflow), .s(result));
  bits_comparator bits_comparator_1 (
    .a(a), .b(b), .is_equal(is_equal), .is_greater(is_greater), .is_shorter(is_shorter));
endmodule
