// Logisim project copy.circ as structural Verilog: 12 circuits, main circuit main
module main (
);

  wire summator_subtractor_1_s0;

  summator_subtractor summator_subtractor_1 (
    .a3(summator_subtractor_1_s0), .s0(summator_subtractor_1_s0));  // open: op, a0, a1, a2, a4, a5, a6, a7, b0, b1, b2, b3, b4, b5, b6, b7, Overflow, s1, s2, s3, s4, s5, s6, s7
endmodule

module summator (
  input  a0,
  input  b0,
  input  c0,
  input  a1,
  input  b1,
  input  a2,
  input  b2,
  input  a3,
  input  b3,
  input  a4,
  input  b4,
  input  a5,
  input  b5,
  input  a6,
  input  b6,
  input  a7,
  input  b7,
  output s0,
  output s1,
  output s2,
  output s3,
  output s4,
  output s5,
  output s6,
  output s7,
  output c7,
  output c8
);

  wire bit_summator_1_count, bit_summator_2_count, bit_summator_3_count, bit_summator_4_count,
       bit_summator_5_count, bit_summator_6_count;

  bit_summator bit_summator_1 (.a(a0), .b(b0), .cin(c0), .s(s0), .count(bit_summator_1_count));
  bit_summator bit_summator_2 (.a(a1), .b(b1), .cin(bit_summator_1_count), .s(s1), .count(bit_summator_2_count));
  bit_summator bit_summator_3 (.a(a2), .b(b2), .cin(bit_summator_2_count), .s(s2), .count(bit_summator_3_count));
  bit_summator bit_summator_4 (.a(a3), .b(b3), .cin(bit_summator_3_count), .s(s3), .count(bit_summator_4_count));
  bit_summator bit_summator_5 (.a(a4), .b(b4), .cin(bit_summator_4_count), .s(s4), .count(bit_summator_5_count));
  bit_summator bit_summator_6 (.a(a5), .b(b5), .cin(bit_summator_5_count), .s(s5), .count(bit_summator_6_count));
  bit_summator bit_summator_7 (.a(a6), .b(b6), .cin(bit_summator_6_count), .s(s6), .count(c7));
  bit_summator bit_summator_8 (.a(a7), .b(b7), .cin(c7), .s(s7), .count(c8));
endmodule

module bit_summator (
  input  a,
  input  b,
  input  cin,
  output s,
  output count
);

  wire and_1_out, and_2_out, and_3_out;

  ExactlyOne xor_1 (.out(s), .in0(a), .in1(b), .in2(cin));
  and and_1 (and_1_out, b, a);
  and and_2 (and_2_out, cin, a);
  and and_3 (and_3_out, b, cin);
  or or_1 (count, and_1_out, and_2_out, and_3_out);
endmodule

module bit_inverter (
  input  should_change,
  input  \bit ,
  output r
);

  xor xor_1 (r, should_change, \bit );
endmodule

module summator_subtractor (
  input  op,
  input  a0,
  input  a1,
  input  a2,
  input  a3,
  input  a4,
  input  a5,
  input  a6,
  input  a7,
  input  b0,
  input  b1,
  input  b2,
  input  b3,
  input  b4,
  input  b5,
  input  b6,
  input  b7,
  output s0,
  output s1,
  output s2,
  output s3,
  output s4,
  output s5,
  output s6,
  output s7,
  output Overflow
);

  wire bit_inverter_1_r, bit_inverter_2_r, bit_inverter_3_r, bit_inverter_4_r, bit_inverter_5_r,
       bit_inverter_6_r, bit_inverter_7_r, bit_inverter_8_r, summator_1_c8;

  bit_inverter bit_inverter_1 (.should_change(b7), .\bit (b0), .r(bit_inverter_1_r));
  bit_inverter bit_inverter_2 (.should_change(b7), .\bit (b1), .r(bit_inverter_2_r));
  bit_inverter bit_inverter_3 (.should_change(b7), .\bit (b2), .r(bit_inverter_3_r));
  bit_inverter bit_inverter_4 (.should_change(b7), .\bit (b3), .r(bit_inverter_4_r));
  bit_inverter bit_inverter_5 (.should_change(b7), .\bit (b4), .r(bit_inverter_5_r));
  bit_inverter bit_inverter_6 (.should_change(b7), .\bit (b5), .r(bit_inverter_6_r));
  bit_inverter bit_inverter_7 (.should_change(b7), .\bit (b6), .r(bit_inverter_7_r));
  bit_inverter bit_inverter_8 (.should_change(b7), .\bit (b7), .r(bit_inverter_8_r));
  summator summator_1 (
    .a0(a0), .b0(bit_inverter_1_r), .c0(b7), .a1(a1), .b1(bit_inverter_2_r), .a2(a2), .b2(bit_inverter_3_r),
    .a3(a3), .b3(bit_inverter_4_r), .a4(a4), .b4(bit_inverter_5_r), .a5(a5), .b5(bit_inverter_6_r), .a6(a6),
    .b6(bit_inverter_7_r), .a7(a7), .b7(bit_inverter_8_r), .s0(s0), .s1(s1), .s2(s2), .s3(s3), .s4(s4),
    .s5(s5), .s6(s6), .s7(s7), .c8(summator_1_c8));  // open: c7
  xor xor_1 (Overflow, summator_1_c8, b7);

  assign op = b7;
endmodule

module bit_comparator (
  input  a,
  input  b,
  input  c,
  output o_ab973f0b,
  output o_dd94291e,
  output o_8c21dccc
);

  wire and_1_out, and_2_out, not_1_out, not_2_out, not_3_out, xor_1_out;

  xor xor_1 (xor_1_out, a, b);
  and and_1 (and_1_out, a, not_1_out);
  not not_1 (not_1_out, b);
  not not_2 (not_2_out, a);
  not not_3 (not_3_out, xor_1_out);
  and and_2 (and_2_out, not_2_out, b);
  and and_3 (o_ab973f0b, not_3_out, c);
  and and_4 (o_dd94291e, and_1_out, c);
  and and_5 (o_8c21dccc, and_2_out, c);
endmodule

module comparator (
  input  a0,
  input  a1,
  input  a2,
  input  a3,
  input  a4,
  input  a5,
  input  a6,
  input  a7,
  input  b0,
  input  b1,
  input  b2,
  input  b3,
  input  b4,
  input  b5,
  input  b6,
  input  b7,
  output o_ab973f0b,
  output o_dd94291e,
  output o_8c21dccc
);

  wire bit_comparator_1_o_8c21dccc, bit_comparator_1_o_ab973f0b, bit_comparator_1_o_dd94291e,
       bit_comparator_2_o_8c21dccc, bit_comparator_2_o_ab973f0b, bit_comparator_2_o_dd94291e,
       bit_comparator_3_o_8c21dccc, bit_comparator_3_o_ab973f0b, bit_comparator_3_o_dd94291e,
       bit_comparator_4_o_8c21dccc, bit_comparator_4_o_ab973f0b, bit_comparator_4_o_dd94291e,
       bit_comparator_5_o_8c21dccc, bit_comparator_5_o_ab973f0b, bit_comparator_5_o_dd94291e,
       bit_comparator_6_o_8c21dccc, bit_comparator_6_o_ab973f0b, bit_comparator_6_o_dd94291e,
       bit_comparator_7_o_8c21dccc, bit_comparator_7_o_ab973f0b, bit_comparator_7_o_dd94291e,
       bit_comparator_8_o_8c21dccc, bit_comparator_8_o_dd94291e;

  bit_comparator bit_comparator_1 (
    .a(a7), .b(b7), .c(1'b1), .o_ab973f0b(bit_comparator_1_o_ab973f0b),
    .o_dd94291e(bit_comparator_1_o_dd94291e), .o_8c21dccc(bit_comparator_1_o_8c21dccc));
  bit_comparator bit_comparator_2 (
    .a(a6), .b(b6), .c(bit_comparator_1_o_ab973f0b), .o_ab973f0b(bit_comparator_2_o_ab973f0b),
    .o_dd94291e(bit_comparator_2_o_dd94291e), .o_8c21dccc(bit_comparator_2_o_8c21dccc));
  bit_comparator bit_comparator_3 (
    .a(a5), .b(b5), .c(bit_comparator_2_o_ab973f0b), .o_ab973f0b(bit_comparator_3_o_ab973f0b),
    .o_dd94291e(bit_comparator_3_o_dd94291e), .o_8c21dccc(bit_comparator_3_o_8c21dccc));
  bit_comparator bit_comparator_4 (
    .a(a4), .b(b4), .c(bit_comparator_3_o_ab973f0b), .o_ab973f0b(bit_comparator_4_o_ab973f0b),
    .o_dd94291e(bit_comparator_4_o_dd94291e), .o_8c21dccc(bit_comparator_4_o_8c21dccc));
  bit_comparator bit_comparator_5 (
    .a(a3), .b(b3), .c(bit_comparator_4_o_ab973f0b), .o_ab973f0b(bit_comparator_5_o_ab973f0b),
    .o_dd94291e(bit_comparator_5_o_dd94291e), .o_8c21dccc(bit_comparator_5_o_8c21dccc));
  bit_comparator bit_comparator_6 (
    .a(a2), .b(b2), .c(bit_comparator_5_o_ab973f0b), .o_ab973f0b(bit_comparator_6_o_ab973f0b),
    .o_dd94291e(bit_comparator_6_o_dd94291e), .o_8c21dccc(bit_comparator_6_o_8c21dccc));
  bit_comparator bit_comparator_7 (
    .a(a1), .b(b1), .c(bit_comparator_6_o_ab973f0b), .o_ab973f0b(bit_comparator_7_o_ab973f0b),
    .o_dd94291e(bit_comparator_7_o_dd94291e), .o_8c21dccc(bit_comparator_7_o_8c21dccc));
  bit_comparator bit_comparator_8 (
    .a(a0), .b(b0), .c(bit_comparator_7_o_ab973f0b), .o_ab973f0b(o_ab973f0b),
    .o_dd94291e(bit_comparator_8_o_dd94291e), .o_8c21dccc(bit_comparator_8_o_8c21dccc));
  or or_1 (o_dd94291e, bit_comparator_8_o_dd94291e, bit_comparator_7_o_dd94291e, bit_comparator_6_o_dd94291e, bit_comparator_5_o_dd94291e, bit_comparator_4_o_dd94291e, bit_comparator_3_o_dd94291e, bit_comparator_2_o_dd94291e, bit_comparator_1_o_dd94291e);
  or or_2 (o_8c21dccc, bit_comparator_8_o_8c21dccc, bit_comparator_7_o_8c21dccc, bit_comparator_6_o_8c21dccc, bit_comparator_5_o_8c21dccc, bit_comparator_4_o_8c21dccc, bit_comparator_3_o_8c21dccc, bit_comparator_2_o_8c21dccc, bit_comparator_1_o_8c21dccc);
endmodule

module ALU (
  input  OP,
  input  a0,
  input  a1,
  input  a2,
  input  a3,
  input  a4,
  input  a5,
  input  a6,
  input  a7,
  input  b0,
  input  b1,
  input  b2,
  input  b3,
  input  b4,
  input  b5,
  input  b6,
  input  b7,
  output s0,
  output s1,
  output s2,
  output s3,
  output s4,
  output s5,
  output s6,
  output s7,
  output Overflow,
  output o_ab973f0b,
  output o_dd94291e,
  output o_8c21dccc
);

  summator_subtractor summator_subtractor_1 (
    .op(OP), .a0(a0), .a1(a1), .a2(a2), .a3(a3), .a4(a4), .a5(a5), .a6(a6), .a7(a7), .b0(b0), .b1(b1),
    .b2(b2), .b3(b3), .b4(b4), .b5(b5), .b6(b6), .b7(b7), .Overflow(Overflow), .s0(s0), .s1(s1), .s2(s2),
    .s3(s3), .s4(s4), .s5(s5), .s6(s6), .s7(s7));
  comparator comparator_1 (
    .a0(a0), .a1(a1), .a2(a2), .a3(a3), .a4(a4), .a5(a5), .a6(a6), .a7(a7), .b0(b0), .b1(b1), .b2(b2),
    .b3(b3), .b4(b4), .b5(b5), .b6(b6), .b7(b7), .o_ab973f0b(o_ab973f0b), .o_dd94291e(o_dd94291e),
    .o_8c21dccc(o_8c21dccc));
endmodule

module bit_ram (
  input  select_value,
  input  input_value,
  input  is_write,
  output output_value
);

  wire and_1_out, and_2_out, not_1_out, not_2_out, not_3_out, not_4_out, or_1_out, or_2_out;

  not not_1 (not_1_out, input_value);
  and and_1 (and_1_out, select_value, not_1_out, is_write);
  and and_2 (and_2_out, select_value, input_value, is_write);
  or or_1 (or_1_out, and_1_out, not_3_out);
  or or_2 (or_2_out, not_2_out, and_2_out);
  not not_2 (not_2_out, or_1_out);
  not not_3 (not_3_out, or_2_out);
  not not_4 (not_4_out, is_write);
  and and_3 (output_value, select_value, not_2_out, not_4_out);
endmodule

module byte_ram (
  input  select_value,
  input  is_write,
  input  a0,
  input  a1,
  input  a2,
  input  a3,
  input  a4,
  input  a5,
  input  a6,
  input  a7,
  output o0,
  output o1,
  output o2,
  output o3,
  output o4,
  output o5,
  output o6,
  output o7
);

  bit_ram bit_ram_1 (.select_value(select_value), .input_value(a0), .is_write(is_write), .output_value(o0));
  bit_ram bit_ram_2 (.select_value(select_value), .input_value(a1), .is_write(is_write), .output_value(o1));
  bit_ram bit_ram_3 (.select_value(select_value), .input_value(a2), .is_write(is_write), .output_value(o2));
  bit_ram bit_ram_4 (.select_value(select_value), .input_value(a3), .is_write(is_write), .output_value(o3));
  bit_ram bit_ram_5 (.select_value(select_value), .input_value(a4), .is_write(is_write), .output_value(o4));
  bit_ram bit_ram_6 (.select_value(select_value), .input_value(a5), .is_write(is_write), .output_value(o5));
  bit_ram bit_ram_7 (.select_value(select_value), .input_value(a6), .is_write(is_write), .output_value(o6));
  bit_ram bit_ram_8 (.select_value(select_value), .input_value(a7), .is_write(is_write), .output_value(o7));
endmodule

module my_RAM (
);

  wire byte_ram_1_o0, byte_ram_2_o0, byte_ram_3_o0, byte_ram_4_o0;

  byte_ram byte_ram_1 (.o0(byte_ram_1_o0));  // open: select_value, is_write, a0, a1, a2, a3, a4, a5, a6, a7, o1, o2, o3, o4, o5, o6, o7
  byte_ram byte_ram_2 (.o0(byte_ram_2_o0));  // open: select_value, is_write, a0, a1, a2, a3, a4, a5, a6, a7, o1, o2, o3, o4, o5, o6, o7
  byte_ram byte_ram_3 (.o0(byte_ram_3_o0));  // open: select_value, is_write, a0, a1, a2, a3, a4, a5, a6, a7, o1, o2, o3, o4, o5, o6, o7
  byte_ram byte_ram_4 (.o0(byte_ram_4_o0));  // open: select_value, is_write, a0, a1, a2, a3, a4, a5, a6, a7, o1, o2, o3, o4, o5, o6, o7
  byte_ram byte_ram_5 ();  // open: select_value, is_write, a0, a1, a2, a3, a4, a5, a6, a7, o0, o1, o2, o3, o4, o5, o6, o7
  byte_ram byte_ram_6 ();  // open: select_value, is_write, a0, a1, a2, a3, a4, a5, a6, a7, o0, o1, o2, o3, o4, o5, o6, o7
  byte_ram byte_ram_7 ();  // open: select_value, is_write, a0, a1, a2, a3, a4, a5, a6, a7, o0, o1, o2, o3, o4, o5, o6, o7
  byte_ram byte_ram_8 ();  // open: select_value, is_write, a0, a1, a2, a3, a4, a5, a6, a7, o0, o1, o2, o3, o4, o5, o6, o7
  byte_ram byte_ram_9 ();  // open: select_value, is_write, a0, a1, a2, a3, a4, a5, a6, a7, o0, o1, o2, o3, o4, o5, o6, o7
  byte_ram byte_ram_10 ();  // open: select_value, is_write, a0, a1, a2, a3, a4, a5, a6, a7, o0, o1, o2, o3, o4, o5, o6, o7
  byte_ram byte_ram_11 ();  // open: select_value, is_write, a0, a1, a2, a3, a4, a5, a6, a7, o0, o1, o2, o3, o4, o5, o6, o7
endmodule

module imense_or_gate (
  input  in_1,
  input  input0,
  input  input1,
  input  input2,
  input  input3,
  input  input4,
  input  input5,
  input  input6,
  input  input7,
  input  input8,
  input  input9,
  input  input10,
  input  input11,
  input  input12,
  input  input13,
  input  input14,
  input  input15,
  input  input16,
  input  input17,
  input  input18,
  input  input19,
  input  input20,
  input  input21,
  input  input22,
  input  input23,
  input  input24,
  input  input25,
  input  input26,
  input  input27,
  input  input28,
  input  input29,
  input  input30,
  input  input31,
  input  input32,
  input  input33,
  input  input34,
  input  input35,
  input  input36,
  input  input37,
  input  input38,
  input  input39,
  input  input40,
  input  input41,
  input  input42,
  input  input43,
  input  input44,
  input  input45,
  input  input46,
  input  input47,
  input  input48,
  input  input49,
  input  input50,
  input  input51,
  input  input52,
  input  input53,
  input  input54,
  input  input55,
  input  input56,
  input  input57,
  input  input58,
  input  input59,
  input  input60,
  input  input61,
  input  input62,
  input  input63,
  input  input64,
  input  input65,
  input  input66,
  input  input67,
  input  input68,
  input  input69,
  input  input70
);

  // OR_Gate or_1 has open pins: in0=input0, in1=input1, in2=input2, in3=input3, in4=input4, in5=input5, in6=input6, in7=input7, in8=input8, in9=input9, in10=input10, in11=input11, in12=input12, in13=input13, in14=input14, in15=input15, in16=input16, in17=input17, in18=input18, in19=input19, in20=input20, in21=input21, in22=input22, in23=input23, in24=input24, in25=input25, in26=input26, in27=input27, in28=input28, in29=input29, in30=input30, in31=input31, out=open
  // OR_Gate or_2 has open pins: in0=input32, in1=input33, in2=input34, in3=input35, in4=input36, in5=input37, in6=input38, in7=input39, in8=input40, in9=input41, in10=input42, in11=input43, in12=input44, in13=input45, in14=input46, in15=input47, in16=input48, in17=input49, in18=input50, in19=input51, in20=input52, in21=input53, in22=input54, in23=input55, in24=input56, in25=input57, in26=input58, in27=input59, in28=input60, in29=input61, in30=input62, in31=input63, out=open
  // OR_Gate or_3 has open pins: in0=input64, in1=input65, in2=input66, in3=input67, in4=input68, in5=input69, in6=input70, out=open
endmodule
