// Logisim project main.circ as structural Verilog: 12 circuits, main circuit main
module main (
  input  [15:0] user_input,
  output overflow,
  output [15:0] main_output,
  output [7:0] output_index
);

  wire alu_1_is_equal, alu_1_is_greater, alu_1_is_shorter, clk_out, uc_1_enable_bus_mux_output,
       uc_1_enable_change_acc, uc_1_enable_change_ir, uc_1_enable_change_pc, uc_1_enable_change_ram,
       uc_1_enable_output_ram, uc_1_enable_print, uc_1_load_pc, uc_1_mux_input_acc, uc_1_mux_input_ram,
       uc_1_op_alu, uc_1_pc_counter_is_up;
  wire [1:0] uc_1_mux_output_ram;
  wire [3:0] IR_q_2;
  wire [11:0] IR_q, multiplexer_1_out, PC_q;
  wire [15:0] ACC_q, alu_1_result, multiplexer_2_out, ram_1_data;

  Clock clk (.out(clk_out));
  Counter #(.width(12), .max('hfff)) PC (
    .clr(1'b0), .load(uc_1_load_pc), .up(uc_1_pc_counter_is_up), .count(uc_1_enable_change_pc),
    .clk(clk_out), .D(IR_q), .Q(PC_q));  // open: carry
  UC uc_1 (
    .clk(clk_out), .instruction(IR_q_2), .is_shorter(alu_1_is_greater), .is_equal(alu_1_is_equal),
    .is_greater(alu_1_is_shorter), .mux_input_acc(uc_1_mux_input_acc), .enable_print(uc_1_enable_print),
    .op_alu(uc_1_op_alu), .mux_output_ram(uc_1_mux_output_ram), .enable_change_acc(uc_1_enable_change_acc),
    .enable_change_ir(uc_1_enable_change_ir), .enable_change_ram(uc_1_enable_change_ram),
    .enable_output_ram(uc_1_enable_output_ram), .mux_input_ram(uc_1_mux_input_ram), .load_PC(uc_1_load_pc),
    .enable_change_PC(uc_1_enable_change_pc), .pc_counter_is_up(uc_1_pc_counter_is_up),
    .enable_bus_mux_output(uc_1_enable_bus_mux_output));
  Register #(.width(16)) IR (.D(ram_1_data), .en(uc_1_enable_change_ir), .clk(clk_out), .Q({IR_q_2, IR_q}), .clr(1'b0));
  ALU alu_1 (
    .OP(uc_1_op_alu), .a(ACC_q), .b(ram_1_data), .result(alu_1_result), .Overflow(overflow),
    .is_equal(alu_1_is_equal), .is_greater(alu_1_is_greater), .is_shorter(alu_1_is_shorter));
  Multiplexer #(.width(12), .enable("false")) multiplexer_1 (
    .in0(PC_q), .in1(IR_q), .out(multiplexer_1_out), .sel(uc_1_mux_input_ram));
  Multiplexer #(.width(16), .enable("false")) multiplexer_2 (
    .in0(ram_1_data), .in1(alu_1_result), .out(multiplexer_2_out), .sel(uc_1_mux_input_acc));
  Register #(.width(16)) ACC (.D(multiplexer_2_out), .en(uc_1_enable_change_acc), .clk(clk_out), .Q(ACC_q), .clr(1'b0));
  RAM #(.addrWidth(12), .dataWidth(16), .trigger("high")) ram_1 (
    .addr(multiplexer_1_out), .we(uc_1_enable_change_ram), .oe(uc_1_enable_output_ram), .data(ram_1_data));
  Multiplexer #(.select(2), .width(16), .disabled("Z")) multiplexer_3 (
    .in0({16{1'b0}}), .in1(ACC_q), .in2(user_input), .in3({{15{1'b0}}, overflow}), .out(ram_1_data),
    .sel(uc_1_mux_output_ram), .en(uc_1_enable_bus_mux_output));
  Register #(.width(16)) register_1 (
    .D(ram_1_data), .en(uc_1_enable_print), .clk(clk_out), .Q(main_output), .clr(1'b0));
  Counter counter_1 (
    .clr(1'b0), .load(1'b0), .up(1'b1), .count(uc_1_enable_print), .clk(clk_out), .Q(output_index));  // open: D, carry

  // Notes on the sheet:
  //   CPU unsigned 16 bit with 12 bit addresses
  //   operation
  //   address
endmodule

module summator (
  input  c0,
  input  [15:0] a,
  input  [15:0] b,
  output [15:0] s,
  output c15,
  output c16
);

  wire bit_summator_1_count, bit_summator_2_count, bit_summator_3_count, bit_summator_4_count,
       bit_summator_5_count, bit_summator_6_count, bit_summator_7_count, bit_summator_8_count,
       bit_summator_9_count, bit_summator_10_count, bit_summator_11_count, bit_summator_12_count,
       bit_summator_13_count, bit_summator_14_count;

  bit_summator bit_summator_1 (.a(a[0]), .b(b[0]), .cin(c0), .s(s[0]), .count(bit_summator_1_count));
  bit_summator bit_summator_2 (.a(a[1]), .b(b[1]), .cin(bit_summator_1_count), .s(s[1]), .count(bit_summator_2_count));
  bit_summator bit_summator_3 (.a(a[2]), .b(b[2]), .cin(bit_summator_2_count), .s(s[2]), .count(bit_summator_3_count));
  bit_summator bit_summator_4 (.a(a[3]), .b(b[3]), .cin(bit_summator_3_count), .s(s[3]), .count(bit_summator_4_count));
  bit_summator bit_summator_5 (.a(a[4]), .b(b[4]), .cin(bit_summator_4_count), .s(s[4]), .count(bit_summator_5_count));
  bit_summator bit_summator_6 (.a(a[5]), .b(b[5]), .cin(bit_summator_5_count), .s(s[5]), .count(bit_summator_6_count));
  bit_summator bit_summator_7 (.a(a[6]), .b(b[6]), .cin(bit_summator_6_count), .s(s[6]), .count(bit_summator_7_count));
  bit_summator bit_summator_8 (.a(a[7]), .b(b[7]), .cin(bit_summator_7_count), .s(s[7]), .count(bit_summator_8_count));
  bit_summator bit_summator_9 (.a(a[8]), .b(b[8]), .cin(bit_summator_8_count), .s(s[8]), .count(bit_summator_9_count));
  bit_summator bit_summator_10 (
    .a(a[9]), .b(b[9]), .cin(bit_summator_9_count), .s(s[9]), .count(bit_summator_10_count));
  bit_summator bit_summator_11 (
    .a(a[10]), .b(b[10]), .cin(bit_summator_10_count), .s(s[10]), .count(bit_summator_11_count));
  bit_summator bit_summator_12 (
    .a(a[11]), .b(b[11]), .cin(bit_summator_11_count), .s(s[11]), .count(bit_summator_12_count));
  bit_summator bit_summator_13 (
    .a(a[12]), .b(b[12]), .cin(bit_summator_12_count), .s(s[12]), .count(bit_summator_13_count));
  bit_summator bit_summator_14 (
    .a(a[13]), .b(b[13]), .cin(bit_summator_13_count), .s(s[13]), .count(bit_summator_14_count));
  bit_summator bit_summator_15 (.a(a[14]), .b(b[14]), .cin(bit_summator_14_count), .s(s[14]), .count(c15));
  bit_summator bit_summator_16 (.a(a[15]), .b(b[15]), .cin(c15), .s(s[15]), .count(c16));
endmodule

module bit_summator (
  input  a,
  input  b,
  input  cin,
  output s,
  output count
);

  wire and_1_out, and_2_out, and_3_out, and_4_out, xor_1_out;

  ExactlyOne xor_1 (.out(xor_1_out), .in0(a), .in1(b), .in2(cin));
  and and_1 (and_1_out, cin, b, a);
  and and_2 (and_2_out, b, a);
  and and_3 (and_3_out, cin, a);
  and and_4 (and_4_out, b, cin);
  or or_1 (s, xor_1_out, and_1_out);
  or or_2 (count, and_2_out, and_3_out, and_4_out);
endmodule

module bit_inverter (
  input  should_change,
  input  \bit ,
  output r
);

  xor xor_1 (r, should_change, \bit );
endmodule

module summator_subtractor (
  input  op,
  input  [15:0] a,
  input  [15:0] b,
  output [15:0] s,
  output Overflow
);

  wire summator_1_c16;
  wire [15:0] bit_inverter_1_r;

  bit_inverter bit_inverter_1 (.should_change(op), .\bit (b[0]), .r(bit_inverter_1_r[0]));
  bit_inverter bit_inverter_2 (.should_change(op), .\bit (b[1]), .r(bit_inverter_1_r[1]));
  bit_inverter bit_inverter_3 (.should_change(op), .\bit (b[2]), .r(bit_inverter_1_r[2]));
  bit_inverter bit_inverter_4 (.should_change(op), .\bit (b[3]), .r(bit_inverter_1_r[3]));
  bit_inverter bit_inverter_5 (.should_change(op), .\bit (b[4]), .r(bit_inverter_1_r[4]));
  bit_inverter bit_inverter_6 (.should_change(op), .\bit (b[5]), .r(bit_inverter_1_r[5]));
  bit_inverter bit_inverter_7 (.should_change(op), .\bit (b[6]), .r(bit_inverter_1_r[6]));
  bit_inverter bit_inverter_8 (.should_change(op), .\bit (b[7]), .r(bit_inverter_1_r[7]));
  bit_inverter bit_inverter_9 (.should_change(op), .\bit (b[8]), .r(bit_inverter_1_r[8]));
  bit_inverter bit_inverter_10 (.should_change(op), .\bit (b[9]), .r(bit_inverter_1_r[9]));
  bit_inverter bit_inverter_11 (.should_change(op), .\bit (b[10]), .r(bit_inverter_1_r[10]));
  bit_inverter bit_inverter_12 (.should_change(op), .\bit (b[11]), .r(bit_inverter_1_r[11]));
  bit_inverter bit_inverter_13 (.should_change(op), .\bit (b[12]), .r(bit_inverter_1_r[12]));
  bit_inverter bit_inverter_14 (.should_change(op), .\bit (b[13]), .r(bit_inverter_1_r[13]));
  bit_inverter bit_inverter_15 (.should_change(op), .\bit (b[14]), .r(bit_inverter_1_r[14]));
  bit_inverter bit_inverter_16 (.should_change(op), .\bit (b[15]), .r(bit_inverter_1_r[15]));
  summator summator_1 (.c0(op), .a(a), .b(bit_inverter_1_r), .s(s), .c16(summator_1_c16));  // open: c15
  xor xor_1 (Overflow, summator_1_c16, op);
endmodule

module bit_comparator (
  input  a,
  input  b,
  input  c,
  output is_equal,
  output is_greater,
  output is_shorter
);

  wire and_1_out, and_2_out, not_1_out, not_2_out, not_3_out, xor_1_out;

  xor xor_1 (xor_1_out, a, b);
  and and_1 (and_1_out, a, not_1_out);
  not not_1 (not_1_out, b);
  not not_2 (not_2_out, a);
  not not_3 (not_3_out, xor_1_out);
  and and_2 (and_2_out, not_2_out, b);
  and and_3 (is_equal, not_3_out, c);
  and and_4 (is_greater, and_1_out, c);
  and and_5 (is_shorter, and_2_out, c);

  // Notes on the sheet:
  //   A relation B
endmodule

module comparator (
  input  [15:0] a,
  input  [15:0] b,
  output is_equal,
  output is_greater,
  output is_shorter
);

  wire bit_comparator_1_is_equal, bit_comparator_1_is_greater, bit_comparator_1_is_shorter,
       bit_comparator_2_is_equal, bit_comparator_2_is_greater, bit_comparator_2_is_shorter,
       bit_comparator_3_is_equal, bit_comparator_3_is_greater, bit_comparator_3_is_shorter,
       bit_comparator_4_is_equal, bit_comparator_4_is_greater, bit_comparator_4_is_shorter,
       bit_comparator_5_is_equal, bit_comparator_5_is_greater, bit_comparator_5_is_shorter,
       bit_comparator_6_is_equal, bit_comparator_6_is_greater, bit_comparator_6_is_shorter,
       bit_comparator_7_is_equal, bit_comparator_7_is_greater, bit_comparator_7_is_shorter,
       bit_comparator_8_is_equal, bit_comparator_8_is_greater, bit_comparator_8_is_shorter,
       bit_comparator_9_is_equal, bit_comparator_9_is_greater, bit_comparator_9_is_shorter,
       bit_comparator_10_is_equal, bit_comparator_10_is_greater, bit_comparator_10_is_shorter,
       bit_comparator_11_is_equal, bit_comparator_11_is_greater, bit_comparator_11_is_shorter,
       bit_comparator_12_is_equal, bit_comparator_12_is_greater, bit_comparator_12_is_shorter,
       bit_comparator_13_is_equal, bit_comparator_13_is_greater, bit_comparator_13_is_shorter,
       bit_comparator_14_is_equal, bit_comparator_14_is_greater, bit_comparator_14_is_shorter,
       bit_comparator_15_is_equal, bit_comparator_15_is_greater, bit_comparator_15_is_shorter,
       bit_comparator_16_is_greater, bit_comparator_16_is_shorter;

  bit_comparator bit_comparator_1 (
    .a(a[15]), .b(b[15]), .c(1'b1), .is_equal(bit_comparator_1_is_equal),
    .is_greater(bit_comparator_1_is_greater), .is_shorter(bit_comparator_1_is_shorter));
  bit_comparator bit_comparator_2 (
    .a(a[14]), .b(b[14]), .c(bit_comparator_1_is_equal), .is_equal(bit_comparator_2_is_equal),
    .is_greater(bit_comparator_2_is_greater), .is_shorter(bit_comparator_2_is_shorter));
  bit_comparator bit_comparator_3 (
    .a(a[13]), .b(b[13]), .c(bit_comparator_2_is_equal), .is_equal(bit_comparator_3_is_equal),
    .is_greater(bit_comparator_3_is_greater), .is_shorter(bit_comparator_3_is_shorter));
  bit_comparator bit_comparator_4 (
    .a(a[12]), .b(b[12]), .c(bit_comparator_3_is_equal), .is_equal(bit_comparator_4_is_equal),
    .is_greater(bit_comparator_4_is_greater), .is_shorter(bit_comparator_4_is_shorter));
  bit_comparator bit_comparator_5 (
    .a(a[11]), .b(b[11]), .c(bit_comparator_4_is_equal), .is_equal(bit_comparator_5_is_equal),
    .is_greater(bit_comparator_5_is_greater), .is_shorter(bit_comparator_5_is_shorter));
  bit_comparator bit_comparator_6 (
    .a(a[10]), .b(b[10]), .c(bit_comparator_5_is_equal), .is_equal(bit_comparator_6_is_equal),
    .is_greater(bit_comparator_6_is_greater), .is_shorter(bit_comparator_6_is_shorter));
  bit_comparator bit_comparator_7 (
    .a(a[9]), .b(b[9]), .c(bit_comparator_6_is_equal), .is_equal(bit_comparator_7_is_equal),
    .is_greater(bit_comparator_7_is_greater), .is_shorter(bit_comparator_7_is_shorter));
  bit_comparator bit_comparator_8 (
    .a(a[8]), .b(b[8]), .c(bit_comparator_7_is_equal), .is_equal(bit_comparator_8_is_equal),
    .is_greater(bit_comparator_8_is_greater), .is_shorter(bit_comparator_8_is_shorter));
  bit_comparator bit_comparator_9 (
    .a(a[7]), .b(b[7]), .c(bit_comparator_8_is_equal), .is_equal(bit_comparator_9_is_equal),
    .is_greater(bit_comparator_9_is_greater), .is_shorter(bit_comparator_9_is_shorter));
  bit_comparator bit_comparator_10 (
    .a(a[6]), .b(b[6]), .c(bit_comparator_9_is_equal), .is_equal(bit_comparator_10_is_equal),
    .is_greater(bit_comparator_10_is_greater), .is_shorter(bit_comparator_10_is_shorter));
  bit_comparator bit_comparator_11 (
    .a(a[5]), .b(b[5]), .c(bit_comparator_10_is_equal), .is_equal(bit_comparator_11_is_equal),
    .is_greater(bit_comparator_11_is_greater), .is_shorter(bit_comparator_11_is_shorter));
  bit_comparator bit_comparator_12 (
    .a(a[4]), .b(b[4]), .c(bit_comparator_11_is_equal), .is_equal(bit_comparator_12_is_equal),
    .is_greater(bit_comparator_12_is_greater), .is_shorter(bit_comparator_12_is_shorter));
  bit_comparator bit_comparator_13 (
    .a(a[3]), .b(b[3]), .c(bit_comparator_12_is_equal), .is_equal(bit_comparator_13_is_equal),
    .is_greater(bit_comparator_13_is_greater), .is_shorter(bit_comparator_13_is_shorter));
  bit_comparator bit_comparator_14 (
    .a(a[2]), .b(b[2]), .c(bit_comparator_13_is_equal), .is_equal(bit_comparator_14_is_equal),
    .is_greater(bit_comparator_14_is_greater), .is_shorter(bit_comparator_14_is_shorter));
  bit_comparator bit_comparator_15 (
    .a(a[1]), .b(b[1]), .c(bit_comparator_14_is_equal), .is_equal(bit_comparator_15_is_equal),
    .is_greater(bit_comparator_15_is_greater), .is_shorter(bit_comparator_15_is_shorter));
  bit_comparator bit_comparator_16 (
    .a(a[0]), .b(b[0]), .c(bit_comparator_15_is_equal), .is_equal(is_equal),
    .is_greater(bit_comparator_16_is_greater), .is_shorter(bit_comparator_16_is_shorter));
  or or_1 (is_greater, bit_comparator_16_is_greater, bit_comparator_15_is_greater, bit_comparator_14_is_greater, bit_comparator_13_is_greater, bit_comparator_12_is_greater, bit_comparator_11_is_greater, bit_comparator_10_is_greater, bit_comparator_9_is_greater, bit_comparator_8_is_greater, bit_comparator_7_is_greater, bit_comparator_6_is_greater, bit_comparator_5_is_greater, bit_comparator_4_is_greater, bit_comparator_3_is_greater, bit_comparator_2_is_greater, bit_comparator_1_is_greater);
  or or_2 (is_shorter, bit_comparator_16_is_shorter, bit_comparator_15_is_shorter, bit_comparator_14_is_shorter, bit_comparator_13_is_shorter, bit_comparator_12_is_shorter, bit_comparator_11_is_shorter, bit_comparator_10_is_shorter, bit_comparator_9_is_shorter, bit_comparator_8_is_shorter, bit_comparator_7_is_shorter, bit_comparator_6_is_shorter, bit_comparator_5_is_shorter, bit_comparator_4_is_shorter, bit_comparator_3_is_shorter, bit_comparator_2_is_shorter, bit_comparator_1_is_shorter);
endmodule

module ALU (
  input  OP,
  input  [15:0] a,
  input  [15:0] b,
  output [15:0] result,
  output Overflow,
  output is_equal,
  output is_greater,
  output is_shorter
);

  summator_subtractor summator_subtractor_1 (.op(OP), .a(a), .b(b), .Overflow(Overflow), .s(result));
  comparator comparator_1 (.a(a), .b(b), .is_equal(is_equal), .is_greater(is_greater), .is_shorter(is_shorter));
endmodule

module bit_ram (
  input  select_value,
  input  input_value,
  input  is_write,
  output output_value
);

  wire and_1_out, and_2_out, not_1_out, not_2_out, not_3_out, not_4_out, or_1_out, or_2_out;

  not not_1 (not_1_out, input_value);
  and and_1 (and_1_out, select_value, not_1_out, is_write);
  and and_2 (and_2_out, select_value, input_value, is_write);
  or or_1 (or_1_out, and_1_out, not_3_out);
  or or_2 (or_2_out, not_2_out, and_2_out);
  not not_2 (not_2_out, or_1_out);
  not not_3 (not_3_out, or_2_out);
  not not_4 (not_4_out, is_write);
  and and_3 (output_value, select_value, not_2_out, not_4_out);
endmodule

module byte_ram (
  input  select_value,
  input  is_write,
  input  a0,
  input  a1,
  input  a2,
  input  a3,
  input  a4,
  input  a5,
  input  a6,
  input  a7,
  output o0,
  output o1,
  output o2,
  output o3,
  output o4,
  output o5,
  output o6,
  output o7
);

  bit_ram bit_ram_1 (.select_value(select_value), .input_value(a0), .is_write(is_write), .output_value(o0));
  bit_ram bit_ram_2 (.select_value(select_value), .input_value(a1), .is_write(is_write), .output_value(o1));
  bit_ram bit_ram_3 (.select_value(select_value), .input_value(a2), .is_write(is_write), .output_value(o2));
  bit_ram bit_ram_4 (.select_value(select_value), .input_value(a3), .is_write(is_write), .output_value(o3));
  bit_ram bit_ram_5 (.select_value(select_value), .input_value(a4), .is_write(is_write), .output_value(o4));
  bit_ram bit_ram_6 (.select_value(select_value), .input_value(a5), .is_write(is_write), .output_value(o5));
  bit_ram bit_ram_7 (.select_value(select_value), .input_value(a6), .is_write(is_write), .output_value(o6));
  bit_ram bit_ram_8 (.select_value(select_value), .input_value(a7), .is_write(is_write), .output_value(o7));
endmodule

module my_RAM (
  input  is_write,
  input  a0,
  input  a1,
  input  a2,
  input  a3,
  input  a4,
  input  a5,
  input  a6,
  input  a7
);

  byte_ram byte_ram_1 (
    .a0(a0), .a1(a1), .a2(a2), .a3(a3), .a4(a4), .a5(a5), .a6(a6), .a7(a7));  // open: select_value, is_write, o0, o1, o2, o3, o4, o5, o6, o7
  byte_ram byte_ram_2 (
    .a0(a0), .a1(a1), .a2(a2), .a3(a3), .a4(a4), .a5(a5), .a6(a6), .a7(a7));  // open: select_value, is_write, o0, o1, o2, o3, o4, o5, o6, o7
  byte_ram byte_ram_3 (
    .a0(a0), .a1(a1), .a2(a2), .a3(a3), .a4(a4), .a5(a5), .a6(a6), .a7(a7));  // open: select_value, is_write, o0, o1, o2, o3, o4, o5, o6, o7
  byte_ram byte_ram_4 (
    .a0(a0), .a1(a1), .a2(a2), .a3(a3), .a4(a4), .a5(a5), .a6(a6), .a7(a7));  // open: select_value, is_write, o0, o1, o2, o3, o4, o5, o6, o7
  byte_ram byte_ram_5 (
    .a0(a0), .a1(a1), .a2(a2), .a3(a3), .a4(a4), .a5(a5), .a6(a6), .a7(a7));  // open: select_value, is_write, o0, o1, o2, o3, o4, o5, o6, o7
  byte_ram byte_ram_6 (
    .a0(a0), .a1(a1), .a2(a2), .a3(a3), .a4(a4), .a5(a5), .a6(a6), .a7(a7));  // open: select_value, is_write, o0, o1, o2, o3, o4, o5, o6, o7
  byte_ram byte_ram_7 (
    .a0(a0), .a1(a1), .a2(a2), .a3(a3), .a4(a4), .a5(a5), .a6(a6), .a7(a7));  // open: select_value, is_write, o0, o1, o2, o3, o4, o5, o6, o7
  byte_ram byte_ram_8 (
    .a0(a0), .a1(a1), .a2(a2), .a3(a3), .a4(a4), .a5(a5), .a6(a6), .a7(a7));  // open: select_value, is_write, o0, o1, o2, o3, o4, o5, o6, o7
  byte_ram byte_ram_9 (
    .a0(a0), .a1(a1), .a2(a2), .a3(a3), .a4(a4), .a5(a5), .a6(a6), .a7(a7));  // open: select_value, is_write, o0, o1, o2, o3, o4, o5, o6, o7
  byte_ram byte_ram_10 (
    .a0(a0), .a1(a1), .a2(a2), .a3(a3), .a4(a4), .a5(a5), .a6(a6), .a7(a7));  // open: select_value, is_write, o0, o1, o2, o3, o4, o5, o6, o7
  byte_ram byte_ram_11 ();  // open: select_value, is_write, a0, a1, a2, a3, a4, a5, a6, a7, o0, o1, o2, o3, o4, o5, o6, o7
  byte_ram byte_ram_12 ();  // open: select_value, is_write, a0, a1, a2, a3, a4, a5, a6, a7, o0, o1, o2, o3, o4, o5, o6, o7
  byte_ram byte_ram_13 ();  // open: select_value, is_write, a0, a1, a2, a3, a4, a5, a6, a7, o0, o1, o2, o3, o4, o5, o6, o7
  byte_ram byte_ram_14 ();  // open: select_value, is_write, a0, a1, a2, a3, a4, a5, a6, a7, o0, o1, o2, o3, o4, o5, o6, o7
  byte_ram byte_ram_15 ();  // open: select_value, is_write, a0, a1, a2, a3, a4, a5, a6, a7, o0, o1, o2, o3, o4, o5, o6, o7
  byte_ram byte_ram_16 ();  // open: select_value, is_write, a0, a1, a2, a3, a4, a5, a6, a7, o0, o1, o2, o3, o4, o5, o6, o7
  byte_ram byte_ram_17 ();  // open: select_value, is_write, a0, a1, a2, a3, a4, a5, a6, a7, o0, o1, o2, o3, o4, o5, o6, o7
  byte_ram byte_ram_18 ();  // open: select_value, is_write, a0, a1, a2, a3, a4, a5, a6, a7, o0, o1, o2, o3, o4, o5, o6, o7
  byte_ram byte_ram_19 ();  // open: select_value, is_write, a0, a1, a2, a3, a4, a5, a6, a7, o0, o1, o2, o3, o4, o5, o6, o7
  byte_ram byte_ram_20 ();  // open: select_value, is_write, a0, a1, a2, a3, a4, a5, a6, a7, o0, o1, o2, o3, o4, o5, o6, o7
  byte_ram byte_ram_21 ();  // open: select_value, is_write, a0, a1, a2, a3, a4, a5, a6, a7, o0, o1, o2, o3, o4, o5, o6, o7
  byte_ram byte_ram_22 ();  // open: select_value, is_write, a0, a1, a2, a3, a4, a5, a6, a7, o0, o1, o2, o3, o4, o5, o6, o7
  byte_ram byte_ram_23 ();  // open: select_value, is_write, a0, a1, a2, a3, a4, a5, a6, a7, o0, o1, o2, o3, o4, o5, o6, o7
  byte_ram byte_ram_24 ();  // open: select_value, is_write, a0, a1, a2, a3, a4, a5, a6, a7, o0, o1, o2, o3, o4, o5, o6, o7
  byte_ram byte_ram_25 ();  // open: select_value, is_write, a0, a1, a2, a3, a4, a5, a6, a7, o0, o1, o2, o3, o4, o5, o6, o7
  byte_ram byte_ram_26 ();  // open: select_value, is_write, a0, a1, a2, a3, a4, a5, a6, a7, o0, o1, o2, o3, o4, o5, o6, o7
  byte_ram byte_ram_27 ();  // open: select_value, is_write, a0, a1, a2, a3, a4, a5, a6, a7, o0, o1, o2, o3, o4, o5, o6, o7
  byte_ram byte_ram_28 ();  // open: select_value, is_write, a0, a1, a2, a3, a4, a5, a6, a7, o0, o1, o2, o3, o4, o5, o6, o7
  byte_ram byte_ram_29 ();  // open: select_value, is_write, a0, a1, a2, a3, a4, a5, a6, a7, o0, o1, o2, o3, o4, o5, o6, o7
  byte_ram byte_ram_30 ();  // open: select_value, is_write, a0, a1, a2, a3, a4, a5, a6, a7, o0, o1, o2, o3, o4, o5, o6, o7
endmodule

module UC (
  input  clk,
  input  [3:0] instruction,
  input  is_shorter,
  input  is_equal,
  input  is_greater,
  output mux_input_acc,
  output enable_print,
  output op_alu,
  output [1:0] mux_output_ram,
  output enable_change_acc,
  output enable_change_ir,
  output enable_change_ram,
  output enable_output_ram,
  output mux_input_ram,
  output load_PC,
  output enable_change_PC,
  output pc_counter_is_up,
  output enable_bus_mux_output
);

  wire t_ff_1_q, t_ff_1_qn;
  wire [3:0] multiplexer_1_out;

  T_Flip_Flop #(.trigger("falling")) t_ff_1 (.T(1'b1), .clk(clk), .Q(t_ff_1_q), .Qn(t_ff_1_qn));  // open: reset, preset
  Multiplexer #(.width(4), .enable("false")) multiplexer_1 (
    .in0(4'b0101), .in1(instruction), .out(multiplexer_1_out), .sel(t_ff_1_q));
  Multiplexer #(.select(4), .width(14), .enable("false")) multiplexer_2 (
    .in0({14{1'b0}}), .in1(14'h130), .in2(14'h251), .in3(14'h2130), .in4(14'h2930), .in5(14'ha6),
    .in6({14{1'b0}}), .in7(14'h451), .in8(14'h1030), .in9(14'h4), .in10(14'hc),
    .in11({{10{1'b0}}, {2{is_shorter}}, 2'b01}), .in12({14{1'b0}}),
    .in13({{10{1'b0}}, {2{is_equal}}, 2'b01}), .in14({14{1'b0}}),
    .in15({{10{1'b0}}, {2{is_greater}}, 2'b01}),
    .out({mux_input_acc, enable_print, op_alu, mux_output_ram, enable_change_acc, enable_change_ir, enable_change_ram, enable_output_ram, mux_input_ram, load_PC, enable_change_PC, pc_counter_is_up, enable_bus_mux_output}),
    .sel(multiplexer_1_out));

  // Notes on the sheet:
  //   fetch
  //   instruction phase
  //   fetch phase
  //   Jump to  to EE if [ACC] > 0
  //   Jump to EE if [ACC]=0
  //   Jump to EE if [ACC] < 0
  //   Store sum [ACC] with [EE] in ACC
  //   Store [ACC] subtracted by [EE] in ACC
  //   ------------------------- FETCH ---------------------
  //   Read number and store in EE
  //   Print [EE]
  //   Stop
  //   Jump to EE
  //   ----
  //   ----
  //   no operation
  //   Copy [EE] to ACC
  //   Copy [ACC] to EE
  //   ----
endmodule
