// Logisim project new.circ as structural Verilog: 12 circuits, main circuit main
module main (
  input  [7:0] user_input,
  output overflow,
  output [7:0] circuit_print,
  output print_enabled
);

  wire alu_1_is_equal, alu_1_is_greater, alu_1_is_shorter, clk_out, uc_1_enable_change_acc,
       uc_1_enable_change_ir, uc_1_enable_change_pc, uc_1_enable_change_ram, uc_1_enable_mux_output,
       uc_1_enable_output_ram, uc_1_load_pc, uc_1_mux_input_ram, uc_1_op_alu, uc_1_pc_counter_is_up;
  wire [1:0] uc_1_dmux_out_ram;
  wire [3:0] IR_q, IR_q_2, multiplexer_1_out, PC_q;
  wire [7:0] ACC_q, alu_1_result, ram_1_data;

  Clock clk (.out(clk_out));
  Clock sysclk ();  // open: out
  Counter #(.width(4), .max('hf)) PC (
    .load(uc_1_load_pc), .up(uc_1_pc_counter_is_up), .count(uc_1_enable_change_pc), .clk(clk_out), .D(IR_q),
    .Q(PC_q));  // open: clr, carry
  UC uc_1 (
    .in_1(clk_out), .instruction(IR_q_2), .is_shorter(alu_1_is_equal), .is_equal(alu_1_is_greater),
    .is_greater(alu_1_is_shorter), .enable_print(print_enabled), .op_alu(uc_1_op_alu),
    .dmux_out_ram(uc_1_dmux_out_ram), .enable_change_acc(uc_1_enable_change_acc),
    .enable_change_ir(uc_1_enable_change_ir), .enable_change_ram(uc_1_enable_change_ram),
    .enable_output_ram(uc_1_enable_output_ram), .mux_input_ram(uc_1_mux_input_ram), .load_PC(uc_1_load_pc),
    .enable_change_PC(uc_1_enable_change_pc), .pc_counter_is_up(uc_1_pc_counter_is_up),
    .enable_mux_output(uc_1_enable_mux_output));
  Register IR (.D(ram_1_data), .en(uc_1_enable_change_ir), .clk(clk_out), .Q({IR_q_2, IR_q}), .clr(1'b0));
  ALU alu_1 (
    .OP(uc_1_op_alu), .a(ACC_q), .b(ram_1_data), .result(alu_1_result), .Overflow(overflow),
    .is_equal(alu_1_is_equal), .is_greater(alu_1_is_greater), .is_shorter(alu_1_is_shorter));
  Register ACC (.D(ram_1_data), .en(uc_1_enable_change_acc), .clk(clk_out), .Q(ACC_q), .clr(1'b0));
  Multiplexer #(.width(4), .enable("false")) multiplexer_1 (
    .in0(PC_q), .in1(IR_q), .out(multiplexer_1_out), .sel(uc_1_mux_input_ram));
  RAM #(.addrWidth(4), .trigger("high")) ram_1 (
    .addr(multiplexer_1_out), .we(uc_1_enable_change_ram), .oe(uc_1_enable_output_ram), .data(ram_1_data));
  Multiplexer #(.select(2), .width(8), .disabled("Z")) multiplexer_2 (
    .in0({8{1'b0}}), .in1(ACC_q), .in2(user_input), .in3(alu_1_result), .out(ram_1_data),
    .sel(uc_1_dmux_out_ram), .en(uc_1_enable_mux_output));
  Multiplexer #(.width(8), .enable("false")) multiplexer_3 (
    .in0({8{1'b1}}), .in1(ram_1_data), .out(circuit_print), .sel(print_enabled));

  // Notes on the sheet:
  //   operation
  //   address
endmodule

module summator (
  input  a0,
  input  b0,
  input  c0,
  input  a1,
  input  b1,
  input  a2,
  input  b2,
  input  a3,
  input  b3,
  input  a4,
  input  b4,
  input  a5,
  input  b5,
  input  a6,
  input  b6,
  input  a7,
  input  b7,
  output s0,
  output s1,
  output s2,
  output s3,
  output s4,
  output s5,
  output s6,
  output s7,
  output c7,
  output c8
);

  wire bit_summator_1_count, bit_summator_2_count, bit_summator_3_count, bit_summator_4_count,
       bit_summator_5_count, bit_summator_6_count;

  bit_summator bit_summator_1 (.a(a0), .b(b0), .cin(c0), .s(s0), .count(bit_summator_1_count));
  bit_summator bit_summator_2 (.a(a1), .b(b1), .cin(bit_summator_1_count), .s(s1), .count(bit_summator_2_count));
  bit_summator bit_summator_3 (.a(a2), .b(b2), .cin(bit_summator_2_count), .s(s2), .count(bit_summator_3_count));
  bit_summator bit_summator_4 (.a(a3), .b(b3), .cin(bit_summator_3_count), .s(s3), .count(bit_summator_4_count));
  bit_summator bit_summator_5 (.a(a4), .b(b4), .cin(bit_summator_4_count), .s(s4), .count(bit_summator_5_count));
  bit_summator bit_summator_6 (.a(a5), .b(b5), .cin(bit_summator_5_count), .s(s5), .count(bit_summator_6_count));
  bit_summator bit_summator_7 (.a(a6), .b(b6), .cin(bit_summator_6_count), .s(s6), .count(c7));
  bit_summator bit_summator_8 (.a(a7), .b(b7), .cin(c7), .s(s7), .count(c8));
endmodule

module bit_summator (
  input  a,
  input  b,
  input  cin,
  output s,
  output count
);

  wire and_1_out, and_2_out, and_3_out;

  ExactlyOne xor_1 (.out(s), .in0(a), .in1(b), .in2(cin));
  and and_1 (and_1_out, b, a);
  and and_2 (and_2_out, cin, a);
  and and_3 (and_3_out, b, cin);
  or or_1 (count, and_1_out, and_2_out, and_3_out);
endmodule

module bit_inverter (
  input  should_change,
  input  \bit ,
  output r
);

  xor xor_1 (r, should_change, \bit );
endmodule

module summator_subtractor (
  input  op,
  input  a0,
  input  a1,
  input  a2,
  input  a3,
  input  a4,
  input  a5,
  input  a6,
  input  a7,
  input  b0,
  input  b1,
  input  b2,
  input  b3,
  input  b4,
  input  b5,
  input  b6,
  input  b7,
  output s0,
  output s1,
  output s2,
  output s3,
  output s4,
  output s5,
  output s6,
  output s7,
  output Overflow
);

  wire bit_inverter_1_r, bit_inverter_2_r, bit_inverter_3_r, bit_inverter_4_r, bit_inverter_5_r,
       bit_inverter_6_r, bit_inverter_7_r, bit_inverter_8_r, summator_1_c8;

  bit_inverter bit_inverter_1 (.should_change(b7), .\bit (b0), .r(bit_inverter_1_r));
  bit_inverter bit_inverter_2 (.should_change(b7), .\bit (b1), .r(bit_inverter_2_r));
  bit_inverter bit_inverter_3 (.should_change(b7), .\bit (b2), .r(bit_inverter_3_r));
  bit_inverter bit_inverter_4 (.should_change(b7), .\bit (b3), .r(bit_inverter_4_r));
  bit_inverter bit_inverter_5 (.should_change(b7), .\bit (b4), .r(bit_inverter_5_r));
  bit_inverter bit_inverter_6 (.should_change(b7), .\bit (b5), .r(bit_inverter_6_r));
  bit_inverter bit_inverter_7 (.should_change(b7), .\bit (b6), .r(bit_inverter_7_r));
  bit_inverter bit_inverter_8 (.should_change(b7), .\bit (b7), .r(bit_inverter_8_r));
  summator summator_1 (
    .a0(a0), .b0(bit_inverter_1_r), .c0(b7), .a1(a1), .b1(bit_inverter_2_r), .a2(a2), .b2(bit_inverter_3_r),
    .a3(a3), .b3(bit_inverter_4_r), .a4(a4), .b4(bit_inverter_5_r), .a5(a5), .b5(bit_inverter_6_r), .a6(a6),
    .b6(bit_inverter_7_r), .a7(a7), .b7(bit_inverter_8_r), .s0(s0), .s1(s1), .s2(s2), .s3(s3), .s4(s4),
    .s5(s5), .s6(s6), .s7(s7), .c8(summator_1_c8));  // open: c7
  xor xor_1 (Overflow, summator_1_c8, b7);

  assign op = b7;
endmodule

module bit_comparator (
  input  a,
  input  b,
  input  c,
  output is_equal,
  output is_greater,
  output is_shorter
);

  wire and_1_out, and_2_out, not_1_out, not_2_out, not_3_out, xor_1_out;

  xor xor_1 (xor_1_out, a, b);
  and and_1 (and_1_out, a, not_1_out);
  not not_1 (not_1_out, b);
  not not_2 (not_2_out, a);
  not not_3 (not_3_out, xor_1_out);
  and and_2 (and_2_out, not_2_out, b);
  and and_3 (is_equal, not_3_out, c);
  and and_4 (is_greater, and_1_out, c);
  and and_5 (is_shorter, and_2_out, c);

  // Notes on the sheet:
  //   A relation B
endmodule

module comparator (
  input  a0,
  input  a1,
  input  a2,
  input  a3,
  input  a4,
  input  a5,
  input  a6,
  input  a7,
  input  b0,
  input  b1,
  input  b2,
  input  b3,
  input  b4,
  input  b5,
  input  b6,
  input  b7,
  output is_equal,
  output is_greater,
  output is_shorter
);

  wire bit_comparator_1_is_equal, bit_comparator_1_is_greater, bit_comparator_1_is_shorter,
       bit_comparator_2_is_equal, bit_comparator_2_is_greater, bit_comparator_2_is_shorter,
       bit_comparator_3_is_equal, bit_comparator_3_is_greater, bit_comparator_3_is_shorter,
       bit_comparator_4_is_equal, bit_comparator_4_is_greater, bit_comparator_4_is_shorter,
       bit_comparator_5_is_equal, bit_comparator_5_is_greater, bit_comparator_5_is_shorter,
       bit_comparator_6_is_equal, bit_comparator_6_is_greater, bit_comparator_6_is_shorter,
       bit_comparator_7_is_equal, bit_comparator_7_is_greater, bit_comparator_7_is_shorter,
       bit_comparator_8_is_greater, bit_comparator_8_is_shorter;

  bit_comparator bit_comparator_1 (
    .a(a7), .b(b7), .c(1'b1), .is_equal(bit_comparator_1_is_equal), .is_greater(bit_comparator_1_is_greater),
    .is_shorter(bit_comparator_1_is_shorter));
  bit_comparator bit_comparator_2 (
    .a(a6), .b(b6), .c(bit_comparator_1_is_equal), .is_equal(bit_comparator_2_is_equal),
    .is_greater(bit_comparator_2_is_greater), .is_shorter(bit_comparator_2_is_shorter));
  bit_comparator bit_comparator_3 (
    .a(a5), .b(b5), .c(bit_comparator_2_is_equal), .is_equal(bit_comparator_3_is_equal),
    .is_greater(bit_comparator_3_is_greater), .is_shorter(bit_comparator_3_is_shorter));
  bit_comparator bit_comparator_4 (
    .a(a4), .b(b4), .c(bit_comparator_3_is_equal), .is_equal(bit_comparator_4_is_equal),
    .is_greater(bit_comparator_4_is_greater), .is_shorter(bit_comparator_4_is_shorter));
  bit_comparator bit_comparator_5 (
    .a(a3), .b(b3), .c(bit_comparator_4_is_equal), .is_equal(bit_comparator_5_is_equal),
    .is_greater(bit_comparator_5_is_greater), .is_shorter(bit_comparator_5_is_shorter));
  bit_comparator bit_comparator_6 (
    .a(a2), .b(b2), .c(bit_comparator_5_is_equal), .is_equal(bit_comparator_6_is_equal),
    .is_greater(bit_comparator_6_is_greater), .is_shorter(bit_comparator_6_is_shorter));
  bit_comparator bit_comparator_7 (
    .a(a1), .b(b1), .c(bit_comparator_6_is_equal), .is_equal(bit_comparator_7_is_equal),
    .is_greater(bit_comparator_7_is_greater), .is_shorter(bit_comparator_7_is_shorter));
  bit_comparator bit_comparator_8 (
    .a(a0), .b(b0), .c(bit_comparator_7_is_equal), .is_equal(is_equal),
    .is_greater(bit_comparator_8_is_greater), .is_shorter(bit_comparator_8_is_shorter));
  or or_1 (is_greater, bit_comparator_8_is_greater, bit_comparator_7_is_greater, bit_comparator_6_is_greater, bit_comparator_5_is_greater, bit_comparator_4_is_greater, bit_comparator_3_is_greater, bit_comparator_2_is_greater, bit_comparator_1_is_greater);
  or or_2 (is_shorter, bit_comparator_8_is_shorter, bit_comparator_7_is_shorter, bit_comparator_6_is_shorter, bit_comparator_5_is_shorter, bit_comparator_4_is_shorter, bit_comparator_3_is_shorter, bit_comparator_2_is_shorter, bit_comparator_1_is_shorter);
endmodule

module ALU (
  input  OP,
  input  [7:0] a,
  input  [7:0] b,
  output [7:0] result,
  output Overflow,
  output is_equal,
  output is_greater,
  output is_shorter
);

  summator_subtractor summator_subtractor_1 (
    .op(OP), .a0(a[0]), .a1(a[1]), .a2(a[2]), .a3(a[3]), .a4(a[4]), .a5(a[5]), .a6(a[6]), .a7(a[7]),
    .b0(b[0]), .b1(b[1]), .b2(b[2]), .b3(b[3]), .b4(b[4]), .b5(b[5]), .b6(b[6]), .b7(b[7]),
    .Overflow(Overflow), .s0(result[0]), .s1(result[1]), .s2(result[2]), .s3(result[3]), .s4(result[4]),
    .s5(result[5]), .s6(result[6]), .s7(result[7]));
  comparator comparator_1 (
    .a0(a[0]), .a1(a[1]), .a2(a[2]), .a3(a[3]), .a4(a[4]), .a5(a[5]), .a6(a[6]), .a7(a[7]), .b0(b[0]),
    .b1(b[1]), .b2(b[2]), .b3(b[3]), .b4(b[4]), .b5(b[5]), .b6(b[6]), .b7(b[7]), .is_equal(is_equal),
    .is_greater(is_greater), .is_shorter(is_shorter));
endmodule

module bit_ram (
  input  select_value,
  input  input_value,
  input  is_write,
  output output_value
);

  wire and_1_out, and_2_out, not_1_out, not_2_out, not_3_out, not_4_out, or_1_out, or_2_out;

  not not_1 (not_1_out, input_value);
  and and_1 (and_1_out, select_value, not_1_out, is_write);
  and and_2 (and_2_out, select_value, input_value, is_write);
  or or_1 (or_1_out, and_1_out, not_3_out);
  or or_2 (or_2_out, not_2_out, and_2_out);
  not not_2 (not_2_out, or_1_out);
  not not_3 (not_3_out, or_2_out);
  not not_4 (not_4_out, is_write);
  and and_3 (output_value, select_value, not_2_out, not_4_out);
endmodule

module byte_ram (
  input  select_value,
  input  is_write,
  input  a0,
  input  a1,
  input  a2,
  input  a3,
  input  a4,
  input  a5,
  input  a6,
  input  a7,
  output o0,
  output o1,
  output o2,
  output o3,
  output o4,
  output o5,
  output o6,
  output o7
);

  bit_ram bit_ram_1 (.select_value(select_value), .input_value(a0), .is_write(is_write), .output_value(o0));
  bit_ram bit_ram_2 (.select_value(select_value), .input_value(a1), .is_write(is_write), .output_value(o1));
  bit_ram bit_ram_3 (.select_value(select_value), .input_value(a2), .is_write(is_write), .output_value(o2));
  bit_ram bit_ram_4 (.select_value(select_value), .input_value(a3), .is_write(is_write), .output_value(o3));
  bit_ram bit_ram_5 (.select_value(select_value), .input_value(a4), .is_write(is_write), .output_value(o4));
  bit_ram bit_ram_6 (.select_value(select_value), .input_value(a5), .is_write(is_write), .output_value(o5));
  bit_ram bit_ram_7 (.select_value(select_value), .input_value(a6), .is_write(is_write), .output_value(o6));
  bit_ram bit_ram_8 (.select_value(select_value), .input_value(a7), .is_write(is_write), .output_value(o7));
endmodule

module my_RAM (
  input  is_write,
  input  a0,
  input  a1,
  input  a2,
  input  a3,
  input  a4,
  input  a5,
  input  a6,
  input  a7
);

  byte_ram byte_ram_1 (
    .a0(a0), .a1(a1), .a2(a2), .a3(a3), .a4(a4), .a5(a5), .a6(a6), .a7(a7));  // open: select_value, is_write, o0, o1, o2, o3, o4, o5, o6, o7
  byte_ram byte_ram_2 (
    .a0(a0), .a1(a1), .a2(a2), .a3(a3), .a4(a4), .a5(a5), .a6(a6), .a7(a7));  // open: select_value, is_write, o0, o1, o2, o3, o4, o5, o6, o7
  byte_ram byte_ram_3 (
    .a0(a0), .a1(a1), .a2(a2), .a3(a3), .a4(a4), .a5(a5), .a6(a6), .a7(a7));  // open: select_value, is_write, o0, o1, o2, o3, o4, o5, o6, o7
  byte_ram byte_ram_4 (
    .a0(a0), .a1(a1), .a2(a2), .a3(a3), .a4(a4), .a5(a5), .a6(a6), .a7(a7));  // open: select_value, is_write, o0, o1, o2, o3, o4, o5, o6, o7
  byte_ram byte_ram_5 (
    .a0(a0), .a1(a1), .a2(a2), .a3(a3), .a4(a4), .a5(a5), .a6(a6), .a7(a7));  // open: select_value, is_write, o0, o1, o2, o3, o4, o5, o6, o7
  byte_ram byte_ram_6 (
    .a0(a0), .a1(a1), .a2(a2), .a3(a3), .a4(a4), .a5(a5), .a6(a6), .a7(a7));  // open: select_value, is_write, o0, o1, o2, o3, o4, o5, o6, o7
  byte_ram byte_ram_7 (
    .a0(a0), .a1(a1), .a2(a2), .a3(a3), .a4(a4), .a5(a5), .a6(a6), .a7(a7));  // open: select_value, is_write, o0, o1, o2, o3, o4, o5, o6, o7
  byte_ram byte_ram_8 (
    .a0(a0), .a1(a1), .a2(a2), .a3(a3), .a4(a4), .a5(a5), .a6(a6), .a7(a7));  // open: select_value, is_write, o0, o1, o2, o3, o4, o5, o6, o7
  byte_ram byte_ram_9 (
    .a0(a0), .a1(a1), .a2(a2), .a3(a3), .a4(a4), .a5(a5), .a6(a6), .a7(a7));  // open: select_value, is_write, o0, o1, o2, o3, o4, o5, o6, o7
  byte_ram byte_ram_10 (
    .a0(a0), .a1(a1), .a2(a2), .a3(a3), .a4(a4), .a5(a5), .a6(a6), .a7(a7));  // open: select_value, is_write, o0, o1, o2, o3, o4, o5, o6, o7
  byte_ram byte_ram_11 ();  // open: select_value, is_write, a0, a1, a2, a3, a4, a5, a6, a7, o0, o1, o2, o3, o4, o5, o6, o7
  byte_ram byte_ram_12 ();  // open: select_value, is_write, a0, a1, a2, a3, a4, a5, a6, a7, o0, o1, o2, o3, o4, o5, o6, o7
  byte_ram byte_ram_13 ();  // open: select_value, is_write, a0, a1, a2, a3, a4, a5, a6, a7, o0, o1, o2, o3, o4, o5, o6, o7
  byte_ram byte_ram_14 ();  // open: select_value, is_write, a0, a1, a2, a3, a4, a5, a6, a7, o0, o1, o2, o3, o4, o5, o6, o7
  byte_ram byte_ram_15 ();  // open: select_value, is_write, a0, a1, a2, a3, a4, a5, a6, a7, o0, o1, o2, o3, o4, o5, o6, o7
  byte_ram byte_ram_16 ();  // open: select_value, is_write, a0, a1, a2, a3, a4, a5, a6, a7, o0, o1, o2, o3, o4, o5, o6, o7
  byte_ram byte_ram_17 ();  // open: select_value, is_write, a0, a1, a2, a3, a4, a5, a6, a7, o0, o1, o2, o3, o4, o5, o6, o7
  byte_ram byte_ram_18 ();  // open: select_value, is_write, a0, a1, a2, a3, a4, a5, a6, a7, o0, o1, o2, o3, o4, o5, o6, o7
  byte_ram byte_ram_19 ();  // open: select_value, is_write, a0, a1, a2, a3, a4, a5, a6, a7, o0, o1, o2, o3, o4, o5, o6, o7
  byte_ram byte_ram_20 ();  // open: select_value, is_write, a0, a1, a2, a3, a4, a5, a6, a7, o0, o1, o2, o3, o4, o5, o6, o7
  byte_ram byte_ram_21 ();  // open: select_value, is_write, a0, a1, a2, a3, a4, a5, a6, a7, o0, o1, o2, o3, o4, o5, o6, o7
  byte_ram byte_ram_22 ();  // open: select_value, is_write, a0, a1, a2, a3, a4, a5, a6, a7, o0, o1, o2, o3, o4, o5, o6, o7
  byte_ram byte_ram_23 ();  // open: select_value, is_write, a0, a1, a2, a3, a4, a5, a6, a7, o0, o1, o2, o3, o4, o5, o6, o7
  byte_ram byte_ram_24 ();  // open: select_value, is_write, a0, a1, a2, a3, a4, a5, a6, a7, o0, o1, o2, o3, o4, o5, o6, o7
  byte_ram byte_ram_25 ();  // open: select_value, is_write, a0, a1, a2, a3, a4, a5, a6, a7, o0, o1, o2, o3, o4, o5, o6, o7
  byte_ram byte_ram_26 ();  // open: select_value, is_write, a0, a1, a2, a3, a4, a5, a6, a7, o0, o1, o2, o3, o4, o5, o6, o7
  byte_ram byte_ram_27 ();  // open: select_value, is_write, a0, a1, a2, a3, a4, a5, a6, a7, o0, o1, o2, o3, o4, o5, o6, o7
  byte_ram byte_ram_28 ();  // open: select_value, is_write, a0, a1, a2, a3, a4, a5, a6, a7, o0, o1, o2, o3, o4, o5, o6, o7
  byte_ram byte_ram_29 ();  // open: select_value, is_write, a0, a1, a2, a3, a4, a5, a6, a7, o0, o1, o2, o3, o4, o5, o6, o7
  byte_ram byte_ram_30 ();  // open: select_value, is_write, a0, a1, a2, a3, a4, a5, a6, a7, o0, o1, o2, o3, o4, o5, o6, o7
endmodule

module UC (
  input  in_1,
  input  [3:0] instruction,
  input  is_shorter,
  input  is_equal,
  input  is_greater,
  output enable_print,
  output op_alu,
  output [1:0] dmux_out_ram,
  output enable_change_acc,
  output enable_change_ir,
  output enable_change_ram,
  output enable_output_ram,
  output mux_input_ram,
  output load_PC,
  output enable_change_PC,
  output pc_counter_is_up,
  output enable_mux_output
);

  wire t_ff_1_q, t_ff_1_qn;
  wire [3:0] multiplexer_1_out;

  T_Flip_Flop t_ff_1 (.T(1'b1), .clk(in_1), .Q(t_ff_1_q), .Qn(t_ff_1_qn));  // open: reset, preset
  Multiplexer #(.width(4), .enable("false")) multiplexer_1 (
    .in0(4'b0101), .in1(instruction), .out(multiplexer_1_out), .sel(t_ff_1_q));
  Multiplexer #(.select(4), .width(13), .enable("false")) multiplexer_2 (
    .in0({13{1'b0}}), .in1(13'h130), .in2({13{1'b1}}), .in3({13{1'b1}}), .in4({13{1'b1}}), .in5(13'ha6),
    .in6({13{1'b0}}), .in7({13{1'b1}}), .in8({13{1'b1}}), .in9({13{1'b1}}), .in10(13'hc),
    .in11({{9{1'b0}}, {2{is_shorter}}, 2'b00}), .in12({13{1'b0}}), .in13({{9{1'b0}}, {2{is_equal}}, 2'b00}),
    .in14({13{1'b0}}), .in15({{9{1'b0}}, {2{is_greater}}, 2'b00}),
    .out({enable_print, op_alu, dmux_out_ram[0], dmux_out_ram[1], enable_change_acc, enable_change_ir, enable_change_ram, enable_output_ram, mux_input_ram, load_PC, enable_change_PC, pc_counter_is_up, enable_mux_output}),
    .sel(multiplexer_1_out));

  // Notes on the sheet:
  //   fetch
  //   instruction phase
  //   fetch phase
  //   Jump to  to EE if [ACC] > 0
  //   Jump to EE if [ACC]=0
  //   Jump to EE if [ACC] < 0
  //   Change [EE] to [AC] + [EE]
  //   Change [EE] to [AC] - [EE]
  //   ------------------------- FETCH ---------------------
  //   Read number and put in [EE]
  //   Print [EE]
  //   Jump to EE
  //   ----
  //   ----
  //   no operation
  //   Copy [EE] to ACC
  //   Copy [ACC] to [EE]
  //   ----
  //   Stop
endmodule
